// Digital circuit FET_4_BIT_ALU_3.dig as structural Verilog
module FET_4_BIT_ALU_3 (
  input  B1,
  input  I2_INV,
  input  Cin,
  input  CLK,
  input  I0_XOR,
  input  I1_AND,
  input  I3_CS,
  input  B2,
  input  B3,
  input  B0,
  output Cout
);

  wire AC0, AC1, AC2, AC3, C1, C2, C3, F0, F1, F2, F3, nfet_1_d, nfet_2_d, nfet_3_d, nfet_4_d, nfet_9_d,
       nfet_10_d, nfet_11_d, nfet_13_s, nfet_15_s, nfet_17_s, nfet_19_s, nfet_21_s, nfet_23_s, nfet_25_s,
       nfet_27_s, nfet_31_d, nfet_32_d, nfet_33_d, nfet_34_d, nfet_35_d, nfet_36_d, nfet_43_d, nfet_44_d,
       nfet_45_s, nfet_47_s, nfet_49_s, nfet_51_s, nfet_53_s, nfet_55_s, nfet_57_s, nfet_59_d, nfet_59_s,
       nfet_61_s, nfet_63_s, nfet_65_s, nfet_67_s, nfet_72_d, nfet_73_s, nfet_75_s, nfet_77_s, nfet_79_s,
       nfet_81_d, nfet_82_d, nfet_82_s, nfet_84_d, nfet_85_d, nfet_85_s, nfet_87_d, nfet_88_d, nfet_88_s,
       nfet_90_d, nfet_90_s, nfet_92_s, nfet_94_d, nfet_95_s, nfet_102_s, nfet_105_s, nfet_113_s, nfet_115_s,
       nfet_117_s, nfet_119_s, nfet_121_d, nfet_121_s, nfet_123_d, nfet_123_s, nfet_125_s, nfet_127_s,
       nfet_129_d, nfet_129_s, nfet_131_s, nfet_133_s, nfet_135_s, nfet_137_d, nfet_137_s, nfet_139_d,
       nfet_139_s, nfet_141_d, nfet_141_s, nfet_143_s, nfet_145_s, nfet_147_d, nfet_147_s, nfet_149_d,
       nfet_150_s, nfet_157_s, nfet_159_s, nfet_161_d, nfet_161_s, nfet_163_d, nfet_163_s, nfet_165_s,
       nfet_167_s, nfet_169_s, nfet_171_s, nfet_173_d, nfet_174_s, nfet_176_d, nfet_177_s, nfet_179_s,
       nfet_181_d, nfet_181_s, nfet_185_s, nfet_187_s, pullup_8_out, pullup_9_out, pullup_10_out,
       pullup_11_out, pullup_12_out, pullup_13_out, pullup_14_out, pullup_21_out, pullup_22_out,
       pullup_25_out, pullup_26_out, pullup_27_out, pullup_33_out, pullup_34_out, pullup_35_out,
       pullup_37_out, pullup_38_out, pullup_39_out, pullup_40_out, pullup_45_out, pullup_46_out,
       pullup_50_out, pullup_52_out, pullup_61_out, pullup_63_out, pullup_65_out, pullup_66_out,
       pullup_68_out, pullup_69_out, pullup_71_out, pullup_74_out, pullup_76_out, pullup_77_out,
       pullup_78_out, pullup_79_out, pullup_80_out, pullup_81_out, pullup_82_out, pullup_83_out,
       pullup_84_out, pullup_85_out, pullup_87_out, pullup_89_out, pullup_90_out, pullup_91_out;

  Seven_Seg_Hex seven_seg_hex_1 (.d({F3, F2, F1, F0}), .dp(1'b0));
  Seven_Seg_Hex seven_seg_hex_2 (.d({AC3, AC2, AC1, AC0}), .dp(1'b0));
  Seven_Seg_Hex seven_seg_hex_3 (.d({B3, B2, B1, B0}), .dp(1'b0));
  NFET nfet_1 (.G(B3), .D(nfet_1_d), .S(1'b0));
  NFET nfet_2 (.G(B2), .D(nfet_2_d), .S(1'b0));
  NFET nfet_3 (.G(B1), .D(nfet_3_d), .S(1'b0));
  PullUp pullup_1 (.out(nfet_1_d));
  PullUp pullup_2 (.out(nfet_2_d));
  NFET nfet_4 (.G(B0), .D(nfet_4_d), .S(1'b0));
  NFET nfet_5 (.G(I2_INV), .D(nfet_1_d), .S(1'b0));
  NFET nfet_6 (.G(I2_INV), .D(nfet_2_d), .S(1'b0));
  PullUp pullup_3 (.out(nfet_3_d));
  NFET nfet_7 (.G(I2_INV), .D(nfet_3_d), .S(1'b0));
  PullUp pullup_4 (.out(nfet_4_d));
  NFET nfet_8 (.G(I2_INV), .D(nfet_4_d), .S(1'b0));
  NFET nfet_9 (.G(nfet_1_d), .D(nfet_9_d), .S(1'b0));
  NFET nfet_10 (.G(nfet_2_d), .D(nfet_10_d), .S(1'b0));
  NFET nfet_11 (.G(nfet_3_d), .D(nfet_11_d), .S(1'b0));
  PullUp pullup_5 (.out(nfet_9_d));
  PullUp pullup_6 (.out(nfet_10_d));
  PullUp pullup_7 (.out(nfet_11_d));
  PullUp pullup_8 (.out(pullup_8_out));
  NFET nfet_12 (.G(nfet_4_d), .D(pullup_8_out), .S(1'b0));
  NFET nfet_13 (.G(B3), .D(nfet_9_d), .S(nfet_13_s));
  NFET nfet_14 (.G(I2_INV), .D(nfet_13_s), .S(1'b0));
  NFET nfet_15 (.G(B2), .D(nfet_10_d), .S(nfet_15_s));
  NFET nfet_16 (.G(I2_INV), .D(nfet_15_s), .S(1'b0));
  NFET nfet_17 (.G(B1), .D(nfet_11_d), .S(nfet_17_s));
  NFET nfet_18 (.G(I2_INV), .D(nfet_17_s), .S(1'b0));
  NFET nfet_19 (.G(B0), .D(pullup_8_out), .S(nfet_19_s));
  NFET nfet_20 (.G(I2_INV), .D(nfet_19_s), .S(1'b0));
  PullUp pullup_9 (.out(pullup_9_out));
  NFET nfet_21 (.G(AC3), .D(pullup_9_out), .S(nfet_21_s));
  NFET nfet_22 (.G(nfet_9_d), .D(nfet_21_s), .S(1'b0));
  PullUp pullup_10 (.out(pullup_10_out));
  NFET nfet_23 (.G(AC2), .D(pullup_10_out), .S(nfet_23_s));
  NFET nfet_24 (.G(nfet_10_d), .D(nfet_23_s), .S(1'b0));
  PullUp pullup_11 (.out(pullup_11_out));
  NFET nfet_25 (.G(AC1), .D(pullup_11_out), .S(nfet_25_s));
  NFET nfet_26 (.G(nfet_11_d), .D(nfet_25_s), .S(1'b0));
  PullUp pullup_12 (.out(pullup_12_out));
  NFET nfet_27 (.G(AC0), .D(pullup_12_out), .S(nfet_27_s));
  NFET nfet_28 (.G(pullup_8_out), .D(nfet_27_s), .S(1'b0));
  PullUp pullup_13 (.out(pullup_13_out));
  NFET nfet_29 (.G(pullup_9_out), .D(pullup_13_out), .S(1'b0));
  PullUp pullup_14 (.out(pullup_14_out));
  NFET nfet_30 (.G(pullup_10_out), .D(pullup_14_out), .S(1'b0));
  NFET nfet_31 (.G(pullup_11_out), .D(nfet_31_d), .S(1'b0));
  NFET nfet_32 (.G(pullup_12_out), .D(nfet_32_d), .S(1'b0));
  PullUp pullup_15 (.out(nfet_31_d));
  PullUp pullup_16 (.out(nfet_32_d));
  NFET nfet_33 (.G(AC3), .D(nfet_33_d), .S(1'b0));
  NFET nfet_34 (.G(AC2), .D(nfet_34_d), .S(1'b0));
  NFET nfet_35 (.G(AC1), .D(nfet_35_d), .S(1'b0));
  NFET nfet_36 (.G(AC0), .D(nfet_36_d), .S(1'b0));
  PullUp pullup_17 (.out(nfet_33_d));
  NFET nfet_37 (.G(nfet_9_d), .D(nfet_33_d), .S(1'b0));
  PullUp pullup_18 (.out(nfet_34_d));
  NFET nfet_38 (.G(nfet_10_d), .D(nfet_34_d), .S(1'b0));
  PullUp pullup_19 (.out(nfet_35_d));
  PullUp pullup_20 (.out(nfet_36_d));
  NFET nfet_39 (.G(nfet_11_d), .D(nfet_35_d), .S(1'b0));
  NFET nfet_40 (.G(pullup_8_out), .D(nfet_36_d), .S(1'b0));
  PullUp pullup_21 (.out(pullup_21_out));
  NFET nfet_41 (.G(nfet_33_d), .D(pullup_21_out), .S(1'b0));
  PullUp pullup_22 (.out(pullup_22_out));
  NFET nfet_42 (.G(nfet_34_d), .D(pullup_22_out), .S(1'b0));
  NFET nfet_43 (.G(nfet_35_d), .D(nfet_43_d), .S(1'b0));
  NFET nfet_44 (.G(nfet_36_d), .D(nfet_44_d), .S(1'b0));
  PullUp pullup_23 (.out(nfet_43_d));
  PullUp pullup_24 (.out(nfet_44_d));
  NFET nfet_45 (.G(AC3), .D(pullup_21_out), .S(nfet_45_s));
  NFET nfet_46 (.G(nfet_9_d), .D(nfet_45_s), .S(1'b0));
  NFET nfet_47 (.G(AC2), .D(pullup_22_out), .S(nfet_47_s));
  NFET nfet_48 (.G(nfet_10_d), .D(nfet_47_s), .S(1'b0));
  NFET nfet_49 (.G(AC1), .D(nfet_43_d), .S(nfet_49_s));
  NFET nfet_50 (.G(nfet_11_d), .D(nfet_49_s), .S(1'b0));
  NFET nfet_51 (.G(AC0), .D(nfet_44_d), .S(nfet_51_s));
  NFET nfet_52 (.G(pullup_8_out), .D(nfet_51_s), .S(1'b0));
  PullUp pullup_25 (.out(pullup_25_out));
  NFET nfet_53 (.G(I0_XOR), .D(pullup_25_out), .S(nfet_53_s));
  NFET nfet_54 (.G(pullup_21_out), .D(nfet_53_s), .S(1'b0));
  PullUp pullup_26 (.out(pullup_26_out));
  NFET nfet_55 (.G(I0_XOR), .D(pullup_26_out), .S(nfet_55_s));
  NFET nfet_56 (.G(pullup_22_out), .D(nfet_55_s), .S(1'b0));
  PullUp pullup_27 (.out(pullup_27_out));
  NFET nfet_57 (.G(I0_XOR), .D(pullup_27_out), .S(nfet_57_s));
  NFET nfet_58 (.G(nfet_43_d), .D(nfet_57_s), .S(1'b0));
  NFET nfet_59 (.G(I0_XOR), .D(nfet_59_d), .S(nfet_59_s));
  NFET nfet_60 (.G(nfet_44_d), .D(nfet_59_s), .S(1'b0));
  PullUp pullup_28 (.out(nfet_59_d));
  PullUp pullup_29 (.out(pullup_25_out));
  NFET nfet_61 (.G(I1_AND), .D(pullup_25_out), .S(nfet_61_s));
  NFET nfet_62 (.G(pullup_13_out), .D(nfet_61_s), .S(1'b0));
  PullUp pullup_30 (.out(pullup_26_out));
  NFET nfet_63 (.G(I1_AND), .D(pullup_26_out), .S(nfet_63_s));
  NFET nfet_64 (.G(pullup_14_out), .D(nfet_63_s), .S(1'b0));
  PullUp pullup_31 (.out(pullup_27_out));
  NFET nfet_65 (.G(I1_AND), .D(pullup_27_out), .S(nfet_65_s));
  NFET nfet_66 (.G(nfet_31_d), .D(nfet_65_s), .S(1'b0));
  PullUp pullup_32 (.out(nfet_59_d));
  NFET nfet_67 (.G(I1_AND), .D(nfet_59_d), .S(nfet_67_s));
  NFET nfet_68 (.G(nfet_32_d), .D(nfet_67_s), .S(1'b0));
  PullUp pullup_33 (.out(pullup_33_out));
  NFET nfet_69 (.G(pullup_25_out), .D(pullup_33_out), .S(1'b0));
  PullUp pullup_34 (.out(pullup_34_out));
  NFET nfet_70 (.G(pullup_26_out), .D(pullup_34_out), .S(1'b0));
  PullUp pullup_35 (.out(pullup_35_out));
  NFET nfet_71 (.G(pullup_27_out), .D(pullup_35_out), .S(1'b0));
  NFET nfet_72 (.G(nfet_59_d), .D(nfet_72_d), .S(1'b0));
  PullUp pullup_36 (.out(nfet_72_d));
  PullUp pullup_37 (.out(pullup_37_out));
  NFET nfet_73 (.G(pullup_33_out), .D(pullup_37_out), .S(nfet_73_s));
  NFET nfet_74 (.G(C3), .D(nfet_73_s), .S(1'b0));
  PullUp pullup_38 (.out(pullup_38_out));
  NFET nfet_75 (.G(pullup_34_out), .D(pullup_38_out), .S(nfet_75_s));
  NFET nfet_76 (.G(C2), .D(nfet_75_s), .S(1'b0));
  PullUp pullup_39 (.out(pullup_39_out));
  NFET nfet_77 (.G(pullup_35_out), .D(pullup_39_out), .S(nfet_77_s));
  NFET nfet_78 (.G(C1), .D(nfet_77_s), .S(1'b0));
  PullUp pullup_40 (.out(pullup_40_out));
  NFET nfet_79 (.G(nfet_72_d), .D(pullup_40_out), .S(nfet_79_s));
  NFET nfet_80 (.G(Cin), .D(nfet_79_s), .S(1'b0));
  NFET nfet_81 (.G(pullup_33_out), .D(nfet_81_d), .S(1'b0));
  NFET nfet_82 (.G(pullup_37_out), .D(nfet_82_d), .S(nfet_82_s));
  NFET nfet_83 (.G(pullup_9_out), .D(nfet_82_s), .S(1'b0));
  NFET nfet_84 (.G(pullup_34_out), .D(nfet_84_d), .S(1'b0));
  NFET nfet_85 (.G(pullup_38_out), .D(nfet_85_d), .S(nfet_85_s));
  NFET nfet_86 (.G(pullup_10_out), .D(nfet_85_s), .S(1'b0));
  NFET nfet_87 (.G(pullup_35_out), .D(nfet_87_d), .S(1'b0));
  PullUp pullup_41 (.out(nfet_81_d));
  PullUp pullup_42 (.out(nfet_82_d));
  NFET nfet_88 (.G(nfet_82_d), .D(nfet_88_d), .S(nfet_88_s));
  NFET nfet_89 (.G(I3_CS), .D(nfet_88_s), .S(1'b0));
  PullUp pullup_43 (.out(nfet_84_d));
  PullUp pullup_44 (.out(nfet_85_d));
  NFET nfet_90 (.G(nfet_85_d), .D(nfet_90_d), .S(nfet_90_s));
  NFET nfet_91 (.G(I3_CS), .D(nfet_90_s), .S(1'b0));
  PullUp pullup_45 (.out(pullup_45_out));
  NFET nfet_92 (.G(pullup_39_out), .D(pullup_45_out), .S(nfet_92_s));
  NFET nfet_93 (.G(pullup_11_out), .D(nfet_92_s), .S(1'b0));
  NFET nfet_94 (.G(nfet_72_d), .D(nfet_94_d), .S(1'b0));
  PullUp pullup_46 (.out(pullup_46_out));
  NFET nfet_95 (.G(pullup_40_out), .D(pullup_46_out), .S(nfet_95_s));
  NFET nfet_96 (.G(pullup_12_out), .D(nfet_95_s), .S(1'b0));
  NFET nfet_97 (.G(C3), .D(nfet_81_d), .S(1'b0));
  NFET nfet_98 (.G(nfet_88_d), .D(Cout), .S(1'b0));
  PullUp pullup_47 (.out(nfet_88_d));
  NFET nfet_99 (.G(C2), .D(nfet_84_d), .S(1'b0));
  NFET nfet_100 (.G(nfet_90_d), .D(C3), .S(1'b0));
  PullUp pullup_48 (.out(nfet_90_d));
  PullUp pullup_49 (.out(nfet_87_d));
  NFET nfet_101 (.G(C1), .D(nfet_87_d), .S(1'b0));
  PullUp pullup_50 (.out(pullup_50_out));
  NFET nfet_102 (.G(pullup_45_out), .D(pullup_50_out), .S(nfet_102_s));
  NFET nfet_103 (.G(I3_CS), .D(nfet_102_s), .S(1'b0));
  PullUp pullup_51 (.out(nfet_94_d));
  NFET nfet_104 (.G(Cin), .D(nfet_94_d), .S(1'b0));
  PullUp pullup_52 (.out(pullup_52_out));
  NFET nfet_105 (.G(pullup_46_out), .D(pullup_52_out), .S(nfet_105_s));
  NFET nfet_106 (.G(I3_CS), .D(nfet_105_s), .S(1'b0));
  NFET nfet_107 (.G(nfet_81_d), .D(F3), .S(1'b0));
  PullUp pullup_53 (.out(Cout));
  NFET nfet_108 (.G(nfet_84_d), .D(F2), .S(1'b0));
  PullUp pullup_54 (.out(C3));
  NFET nfet_109 (.G(nfet_87_d), .D(F1), .S(1'b0));
  PullUp pullup_55 (.out(C2));
  NFET nfet_110 (.G(pullup_50_out), .D(C2), .S(1'b0));
  NFET nfet_111 (.G(pullup_52_out), .D(C1), .S(1'b0));
  NFET nfet_112 (.G(nfet_94_d), .D(F0), .S(1'b0));
  PullUp pullup_56 (.out(C1));
  PullUp pullup_57 (.out(F3));
  PullUp pullup_58 (.out(F2));
  PullUp pullup_59 (.out(F1));
  PullUp pullup_60 (.out(F0));
  NFET nfet_113 (.G(pullup_33_out), .D(F3), .S(nfet_113_s));
  NFET nfet_114 (.G(C3), .D(nfet_113_s), .S(1'b0));
  NFET nfet_115 (.G(pullup_34_out), .D(F2), .S(nfet_115_s));
  NFET nfet_116 (.G(C2), .D(nfet_115_s), .S(1'b0));
  NFET nfet_117 (.G(pullup_35_out), .D(F1), .S(nfet_117_s));
  NFET nfet_118 (.G(C1), .D(nfet_117_s), .S(1'b0));
  NFET nfet_119 (.G(nfet_72_d), .D(F0), .S(nfet_119_s));
  NFET nfet_120 (.G(Cin), .D(nfet_119_s), .S(1'b0));
  NFET nfet_121 (.G(CLK), .D(nfet_121_d), .S(nfet_121_s));
  NFET nfet_122 (.G(nfet_137_d), .D(nfet_121_s), .S(1'b0));
  NFET nfet_123 (.G(CLK), .D(nfet_123_d), .S(nfet_123_s));
  NFET nfet_124 (.G(nfet_139_d), .D(nfet_123_s), .S(1'b0));
  PullUp pullup_61 (.out(pullup_61_out));
  NFET nfet_125 (.G(pullup_69_out), .D(pullup_61_out), .S(nfet_125_s));
  PullUp pullup_62 (.out(nfet_121_d));
  NFET nfet_126 (.G(nfet_121_d), .D(nfet_125_s), .S(1'b0));
  PullUp pullup_63 (.out(pullup_63_out));
  NFET nfet_127 (.G(pullup_71_out), .D(pullup_63_out), .S(nfet_127_s));
  PullUp pullup_64 (.out(nfet_123_d));
  NFET nfet_128 (.G(nfet_123_d), .D(nfet_127_s), .S(1'b0));
  NFET nfet_129 (.G(nfet_147_d), .D(nfet_129_d), .S(nfet_129_s));
  PullUp pullup_65 (.out(pullup_65_out));
  NFET nfet_130 (.G(pullup_65_out), .D(nfet_129_s), .S(1'b0));
  NFET nfet_131 (.G(CLK), .D(pullup_65_out), .S(nfet_131_s));
  NFET nfet_132 (.G(nfet_141_d), .D(nfet_131_s), .S(1'b0));
  PullUp pullup_66 (.out(pullup_66_out));
  NFET nfet_133 (.G(CLK), .D(pullup_66_out), .S(nfet_133_s));
  NFET nfet_134 (.G(pullup_74_out), .D(nfet_133_s), .S(1'b0));
  PullUp pullup_67 (.out(nfet_129_d));
  PullUp pullup_68 (.out(pullup_68_out));
  NFET nfet_135 (.G(pullup_76_out), .D(pullup_68_out), .S(nfet_135_s));
  NFET nfet_136 (.G(pullup_66_out), .D(nfet_135_s), .S(1'b0));
  NFET nfet_137 (.G(CLK), .D(nfet_137_d), .S(nfet_137_s));
  NFET nfet_138 (.G(F3), .D(nfet_137_s), .S(1'b0));
  NFET nfet_139 (.G(CLK), .D(nfet_139_d), .S(nfet_139_s));
  NFET nfet_140 (.G(F2), .D(nfet_139_s), .S(1'b0));
  NFET nfet_141 (.G(CLK), .D(nfet_141_d), .S(nfet_141_s));
  NFET nfet_142 (.G(F1), .D(nfet_141_s), .S(1'b0));
  PullUp pullup_69 (.out(pullup_69_out));
  NFET nfet_143 (.G(pullup_61_out), .D(pullup_69_out), .S(nfet_143_s));
  PullUp pullup_70 (.out(nfet_137_d));
  NFET nfet_144 (.G(nfet_137_d), .D(nfet_143_s), .S(1'b0));
  PullUp pullup_71 (.out(pullup_71_out));
  NFET nfet_145 (.G(pullup_63_out), .D(pullup_71_out), .S(nfet_145_s));
  PullUp pullup_72 (.out(nfet_139_d));
  NFET nfet_146 (.G(nfet_139_d), .D(nfet_145_s), .S(1'b0));
  NFET nfet_147 (.G(nfet_129_d), .D(nfet_147_d), .S(nfet_147_s));
  PullUp pullup_73 (.out(nfet_141_d));
  NFET nfet_148 (.G(nfet_141_d), .D(nfet_147_s), .S(1'b0));
  PullUp pullup_74 (.out(pullup_74_out));
  NFET nfet_149 (.G(pullup_74_out), .D(nfet_149_d), .S(1'b0));
  NFET nfet_150 (.G(CLK), .D(pullup_74_out), .S(nfet_150_s));
  NFET nfet_151 (.G(F0), .D(nfet_150_s), .S(1'b0));
  PullUp pullup_75 (.out(nfet_147_d));
  PullUp pullup_76 (.out(pullup_76_out));
  NFET nfet_152 (.G(pullup_68_out), .D(pullup_76_out), .S(nfet_149_d));
  PullUp pullup_77 (.out(pullup_77_out));
  NFET nfet_153 (.G(CLK), .D(pullup_77_out), .S(1'b0));
  PullUp pullup_78 (.out(pullup_78_out));
  NFET nfet_154 (.G(CLK), .D(pullup_78_out), .S(1'b0));
  PullUp pullup_79 (.out(pullup_79_out));
  NFET nfet_155 (.G(CLK), .D(pullup_79_out), .S(1'b0));
  PullUp pullup_80 (.out(pullup_80_out));
  NFET nfet_156 (.G(CLK), .D(pullup_80_out), .S(1'b0));
  PullUp pullup_81 (.out(pullup_81_out));
  NFET nfet_157 (.G(pullup_77_out), .D(pullup_81_out), .S(nfet_157_s));
  NFET nfet_158 (.G(pullup_61_out), .D(nfet_157_s), .S(1'b0));
  PullUp pullup_82 (.out(pullup_82_out));
  NFET nfet_159 (.G(pullup_78_out), .D(pullup_82_out), .S(nfet_159_s));
  NFET nfet_160 (.G(pullup_63_out), .D(nfet_159_s), .S(1'b0));
  NFET nfet_161 (.G(pullup_79_out), .D(nfet_161_d), .S(nfet_161_s));
  NFET nfet_162 (.G(nfet_129_d), .D(nfet_161_s), .S(1'b0));
  NFET nfet_163 (.G(pullup_80_out), .D(nfet_163_d), .S(nfet_163_s));
  NFET nfet_164 (.G(pullup_68_out), .D(nfet_163_s), .S(1'b0));
  PullUp pullup_83 (.out(pullup_83_out));
  NFET nfet_165 (.G(AC3), .D(pullup_83_out), .S(nfet_165_s));
  NFET nfet_166 (.G(pullup_81_out), .D(nfet_165_s), .S(1'b0));
  PullUp pullup_84 (.out(pullup_84_out));
  NFET nfet_167 (.G(AC2), .D(pullup_84_out), .S(nfet_167_s));
  NFET nfet_168 (.G(pullup_82_out), .D(nfet_167_s), .S(1'b0));
  PullUp pullup_85 (.out(pullup_85_out));
  NFET nfet_169 (.G(AC1), .D(pullup_85_out), .S(nfet_169_s));
  PullUp pullup_86 (.out(nfet_161_d));
  NFET nfet_170 (.G(nfet_161_d), .D(nfet_169_s), .S(1'b0));
  PullUp pullup_87 (.out(pullup_87_out));
  NFET nfet_171 (.G(AC0), .D(pullup_87_out), .S(nfet_171_s));
  PullUp pullup_88 (.out(nfet_163_d));
  NFET nfet_172 (.G(nfet_163_d), .D(nfet_171_s), .S(1'b0));
  PullUp pullup_89 (.out(pullup_89_out));
  NFET nfet_173 (.G(pullup_89_out), .D(nfet_173_d), .S(1'b0));
  NFET nfet_174 (.G(pullup_77_out), .D(pullup_89_out), .S(nfet_174_s));
  NFET nfet_175 (.G(pullup_69_out), .D(nfet_174_s), .S(1'b0));
  PullUp pullup_90 (.out(pullup_90_out));
  NFET nfet_176 (.G(pullup_90_out), .D(nfet_176_d), .S(1'b0));
  NFET nfet_177 (.G(pullup_78_out), .D(pullup_90_out), .S(nfet_177_s));
  NFET nfet_178 (.G(pullup_71_out), .D(nfet_177_s), .S(1'b0));
  PullUp pullup_91 (.out(pullup_91_out));
  NFET nfet_179 (.G(pullup_79_out), .D(pullup_91_out), .S(nfet_179_s));
  NFET nfet_180 (.G(nfet_147_d), .D(nfet_179_s), .S(1'b0));
  NFET nfet_181 (.G(pullup_80_out), .D(nfet_181_d), .S(nfet_181_s));
  NFET nfet_182 (.G(pullup_76_out), .D(nfet_181_s), .S(1'b0));
  PullUp pullup_92 (.out(AC3));
  NFET nfet_183 (.G(pullup_83_out), .D(AC3), .S(nfet_173_d));
  PullUp pullup_93 (.out(AC2));
  NFET nfet_184 (.G(pullup_84_out), .D(AC2), .S(nfet_176_d));
  PullUp pullup_94 (.out(AC1));
  NFET nfet_185 (.G(pullup_85_out), .D(AC1), .S(nfet_185_s));
  NFET nfet_186 (.G(pullup_91_out), .D(nfet_185_s), .S(1'b0));
  PullUp pullup_95 (.out(AC0));
  NFET nfet_187 (.G(pullup_87_out), .D(AC0), .S(nfet_187_s));
  PullUp pullup_96 (.out(nfet_181_d));
  NFET nfet_188 (.G(nfet_181_d), .D(nfet_187_s), .S(1'b0));

  // Other names for the same wires on the sheet: C4 = Cout

  // Notes on the sheet:
  //   ALU
  //   ACC
  //   BUS
endmodule
