// Digital circuit NMOS_FET_Gates.dig as structural Verilog
module NMOS_FET_Gates (
  input  in_1,
  input  in_2,
  input  in_4,
  input  in_5,
  input  A,
  input  B,
  input  Din,
  input  CLK,
  input  A_2,
  input  B_2,
  input  A_3,
  input  B_3,
  input  Cin,
  input  A_4,
  input  SEL,
  input  B_4,
  input  B_5,
  input  I2,
  input  Cin_2,
  input  CLK_2,
  input  I0,
  input  I1,
  input  I3_CS,
  output out_3,
  output out_6,
  output Sum,
  output Cout,
  output Q0ut,
  output Fout,
  output Sum_2,
  output Cout_2,
  output Out,
  output Cout_3,
  output Qout
);

  wire nfet_1_d, nfet_2_s, nfet_4_s, nfet_6_s, nfet_8_s, nfet_10_d, nfet_12_d, nfet_14_d, nfet_16_s,
       nfet_19_d, nfet_21_d, nfet_26_s, nfet_29_s, nfet_32_s, nfet_34_s, nfet_36_s, nfet_38_d, nfet_39_s,
       nfet_41_d, nfet_42_d, nfet_46_d, nfet_46_s, nfet_48_d, nfet_49_s, nfet_51_s, nfet_53_s, nfet_55_s,
       nfet_57_s, nfet_59_s, nfet_61_s, nfet_64_s, nfet_66_d, nfet_66_s, nfet_68_s, nfet_71_d, nfet_71_s,
       nfet_73_s, nfet_75_s, nfet_77_d, nfet_78_d, nfet_78_s, nfet_80_s, nfet_83_d, nfet_84_s, nfet_86_d,
       nfet_86_s, nfet_88_s, nfet_90_d, nfet_90_s, nfet_92_s, nfet_95_s, nfet_97_s, nfet_99_d, nfet_100_s,
       pullup_2_out, pullup_3_out, pullup_4_out, pullup_15_out, pullup_18_out, pullup_19_out, pullup_23_out,
       pullup_28_out, pullup_29_out, pullup_30_out, pullup_31_out, pullup_33_out, pullup_35_out,
       pullup_36_out, pullup_43_out, pullup_45_out, pullup_47_out, pullup_48_out, pullup_49_out,
       pullup_50_out;

  NFET nfet_1 (.G(SEL), .D(nfet_1_d), .S(1'b0));
  LED u_Fout (.in(nfet_83_d));
  PullUp pullup_1 (.out(nfet_1_d));
  PullUp pullup_2 (.out(pullup_2_out));
  NFET nfet_2 (.G(A), .D(pullup_2_out), .S(nfet_2_s));
  NFET nfet_3 (.G(B), .D(nfet_2_s), .S(1'b0));
  PullUp pullup_3 (.out(pullup_3_out));
  NFET nfet_4 (.G(A_3), .D(pullup_3_out), .S(nfet_4_s));
  NFET nfet_5 (.G(B_3), .D(nfet_4_s), .S(1'b0));
  PullUp pullup_4 (.out(pullup_4_out));
  NFET nfet_6 (.G(SEL), .D(pullup_4_out), .S(nfet_6_s));
  NFET nfet_7 (.G(A_4), .D(nfet_6_s), .S(1'b0));
  PullUp pullup_5 (.out(out_3));
  NFET nfet_8 (.G(in_1), .D(out_3), .S(nfet_8_s));
  NFET nfet_9 (.G(in_2), .D(nfet_8_s), .S(1'b0));
  NFET nfet_10 (.G(A_2), .D(nfet_10_d), .S(1'b0));
  NFET nfet_11 (.G(pullup_2_out), .D(Cout), .S(1'b0));
  NFET nfet_12 (.G(B_5), .D(nfet_12_d), .S(1'b0));
  PullUp pullup_6 (.out(Cout));
  PullUp pullup_7 (.out(nfet_10_d));
  NFET nfet_13 (.G(B_2), .D(nfet_10_d), .S(1'b0));
  NFET nfet_14 (.G(A_3), .D(nfet_14_d), .S(1'b0));
  PullUp pullup_8 (.out(nfet_12_d));
  NFET nfet_15 (.G(I2), .D(nfet_12_d), .S(1'b0));
  PullUp pullup_9 (.out(pullup_4_out));
  NFET nfet_16 (.G(nfet_1_d), .D(pullup_4_out), .S(nfet_16_s));
  NFET nfet_17 (.G(B_4), .D(nfet_16_s), .S(1'b0));
  NFET nfet_18 (.G(nfet_10_d), .D(Fout), .S(1'b0));
  NFET nfet_19 (.G(A), .D(nfet_19_d), .S(1'b0));
  PullUp pullup_10 (.out(nfet_14_d));
  NFET nfet_20 (.G(B_3), .D(nfet_14_d), .S(1'b0));
  NFET nfet_21 (.G(nfet_12_d), .D(nfet_21_d), .S(1'b0));
  PullUp pullup_11 (.out(Fout));
  PullUp pullup_12 (.out(nfet_19_d));
  PullUp pullup_13 (.out(nfet_21_d));
  PullUp pullup_14 (.out(Out));
  NFET nfet_22 (.G(pullup_4_out), .D(Out), .S(1'b0));
  NFET nfet_23 (.G(in_4), .D(out_6), .S(1'b0));
  NFET nfet_24 (.G(B), .D(nfet_19_d), .S(1'b0));
  PullUp pullup_15 (.out(pullup_15_out));
  NFET nfet_25 (.G(nfet_14_d), .D(pullup_15_out), .S(1'b0));
  PullUp pullup_16 (.out(out_6));
  NFET nfet_26 (.G(A_2), .D(Fout), .S(nfet_26_s));
  NFET nfet_27 (.G(B_2), .D(nfet_26_s), .S(1'b0));
  NFET nfet_28 (.G(nfet_19_d), .D(Sum), .S(1'b0));
  NFET nfet_29 (.G(B_5), .D(nfet_21_d), .S(nfet_29_s));
  NFET nfet_30 (.G(I2), .D(nfet_29_s), .S(1'b0));
  NFET nfet_31 (.G(in_5), .D(out_6), .S(1'b0));
  PullUp pullup_17 (.out(Sum));
  NFET nfet_32 (.G(A_3), .D(pullup_15_out), .S(nfet_32_s));
  NFET nfet_33 (.G(B_3), .D(nfet_32_s), .S(1'b0));
  PullUp pullup_18 (.out(pullup_18_out));
  NFET nfet_34 (.G(Qout), .D(pullup_18_out), .S(nfet_34_s));
  NFET nfet_35 (.G(nfet_21_d), .D(nfet_34_s), .S(1'b0));
  NFET nfet_36 (.G(A), .D(Sum), .S(nfet_36_s));
  NFET nfet_37 (.G(B), .D(nfet_36_s), .S(1'b0));
  NFET nfet_38 (.G(pullup_18_out), .D(nfet_38_d), .S(1'b0));
  PullUp pullup_19 (.out(pullup_19_out));
  NFET nfet_39 (.G(pullup_15_out), .D(pullup_19_out), .S(nfet_39_s));
  NFET nfet_40 (.G(Cin), .D(nfet_39_s), .S(1'b0));
  PullUp pullup_20 (.out(nfet_38_d));
  NFET nfet_41 (.G(pullup_15_out), .D(nfet_41_d), .S(1'b0));
  NFET nfet_42 (.G(Qout), .D(nfet_42_d), .S(1'b0));
  PullUp pullup_21 (.out(nfet_41_d));
  NFET nfet_43 (.G(Cin), .D(nfet_41_d), .S(1'b0));
  PullUp pullup_22 (.out(nfet_42_d));
  NFET nfet_44 (.G(nfet_41_d), .D(Sum_2), .S(1'b0));
  NFET nfet_45 (.G(nfet_21_d), .D(nfet_42_d), .S(1'b0));
  NFET nfet_46 (.G(CLK), .D(nfet_46_d), .S(nfet_46_s));
  NFET nfet_47 (.G(pullup_28_out), .D(nfet_46_s), .S(1'b0));
  NFET nfet_48 (.G(nfet_42_d), .D(nfet_48_d), .S(1'b0));
  PullUp pullup_23 (.out(pullup_23_out));
  NFET nfet_49 (.G(pullup_29_out), .D(pullup_23_out), .S(nfet_49_s));
  PullUp pullup_24 (.out(nfet_46_d));
  NFET nfet_50 (.G(nfet_46_d), .D(nfet_49_s), .S(1'b0));
  PullUp pullup_25 (.out(Sum_2));
  PullUp pullup_26 (.out(nfet_48_d));
  NFET nfet_51 (.G(pullup_15_out), .D(Sum_2), .S(nfet_51_s));
  NFET nfet_52 (.G(Cin), .D(nfet_51_s), .S(1'b0));
  PullUp pullup_27 (.out(Cout_2));
  NFET nfet_53 (.G(pullup_19_out), .D(Cout_2), .S(nfet_53_s));
  NFET nfet_54 (.G(pullup_3_out), .D(nfet_53_s), .S(1'b0));
  PullUp pullup_28 (.out(pullup_28_out));
  NFET nfet_55 (.G(CLK), .D(pullup_28_out), .S(nfet_55_s));
  NFET nfet_56 (.G(Din), .D(nfet_55_s), .S(1'b0));
  NFET nfet_57 (.G(Qout), .D(nfet_48_d), .S(nfet_57_s));
  NFET nfet_58 (.G(nfet_21_d), .D(nfet_57_s), .S(1'b0));
  PullUp pullup_29 (.out(pullup_29_out));
  NFET nfet_59 (.G(pullup_23_out), .D(pullup_29_out), .S(nfet_59_s));
  NFET nfet_60 (.G(pullup_28_out), .D(nfet_59_s), .S(1'b0));
  PullUp pullup_30 (.out(pullup_30_out));
  NFET nfet_61 (.G(I0), .D(pullup_30_out), .S(nfet_61_s));
  NFET nfet_62 (.G(nfet_48_d), .D(nfet_61_s), .S(1'b0));
  PullUp pullup_31 (.out(pullup_31_out));
  NFET nfet_63 (.G(CLK), .D(pullup_31_out), .S(1'b0));
  PullUp pullup_32 (.out(pullup_30_out));
  NFET nfet_64 (.G(I1), .D(pullup_30_out), .S(nfet_64_s));
  NFET nfet_65 (.G(nfet_38_d), .D(nfet_64_s), .S(1'b0));
  NFET nfet_66 (.G(pullup_31_out), .D(nfet_66_d), .S(nfet_66_s));
  NFET nfet_67 (.G(pullup_23_out), .D(nfet_66_s), .S(1'b0));
  PullUp pullup_33 (.out(pullup_33_out));
  NFET nfet_68 (.G(Q0ut), .D(pullup_33_out), .S(nfet_68_s));
  PullUp pullup_34 (.out(nfet_66_d));
  NFET nfet_69 (.G(nfet_66_d), .D(nfet_68_s), .S(1'b0));
  PullUp pullup_35 (.out(pullup_35_out));
  NFET nfet_70 (.G(pullup_30_out), .D(pullup_35_out), .S(1'b0));
  NFET nfet_71 (.G(pullup_31_out), .D(nfet_71_d), .S(nfet_71_s));
  NFET nfet_72 (.G(pullup_29_out), .D(nfet_71_s), .S(1'b0));
  PullUp pullup_36 (.out(pullup_36_out));
  NFET nfet_73 (.G(pullup_35_out), .D(pullup_36_out), .S(nfet_73_s));
  NFET nfet_74 (.G(Cin_2), .D(nfet_73_s), .S(1'b0));
  PullUp pullup_37 (.out(Q0ut));
  NFET nfet_75 (.G(pullup_33_out), .D(Q0ut), .S(nfet_75_s));
  PullUp pullup_38 (.out(nfet_71_d));
  NFET nfet_76 (.G(nfet_71_d), .D(nfet_75_s), .S(1'b0));
  NFET nfet_77 (.G(pullup_35_out), .D(nfet_77_d), .S(1'b0));
  NFET nfet_78 (.G(pullup_36_out), .D(nfet_78_d), .S(nfet_78_s));
  NFET nfet_79 (.G(pullup_18_out), .D(nfet_78_s), .S(1'b0));
  PullUp pullup_39 (.out(nfet_77_d));
  PullUp pullup_40 (.out(nfet_78_d));
  NFET nfet_80 (.G(nfet_78_d), .D(Cout_3), .S(nfet_80_s));
  NFET nfet_81 (.G(I3_CS), .D(nfet_80_s), .S(1'b0));
  NFET nfet_82 (.G(Cin_2), .D(nfet_77_d), .S(1'b0));
  PullUp pullup_41 (.out(Cout_3));
  NFET nfet_83 (.G(nfet_77_d), .D(nfet_83_d), .S(1'b0));
  PullUp pullup_42 (.out(nfet_83_d));
  NFET nfet_84 (.G(pullup_35_out), .D(nfet_83_d), .S(nfet_84_s));
  NFET nfet_85 (.G(Cin_2), .D(nfet_84_s), .S(1'b0));
  NFET nfet_86 (.G(CLK_2), .D(nfet_86_d), .S(nfet_86_s));
  NFET nfet_87 (.G(nfet_90_d), .D(nfet_86_s), .S(1'b0));
  PullUp pullup_43 (.out(pullup_43_out));
  NFET nfet_88 (.G(pullup_45_out), .D(pullup_43_out), .S(nfet_88_s));
  PullUp pullup_44 (.out(nfet_86_d));
  NFET nfet_89 (.G(nfet_86_d), .D(nfet_88_s), .S(1'b0));
  NFET nfet_90 (.G(CLK_2), .D(nfet_90_d), .S(nfet_90_s));
  NFET nfet_91 (.G(nfet_83_d), .D(nfet_90_s), .S(1'b0));
  PullUp pullup_45 (.out(pullup_45_out));
  NFET nfet_92 (.G(pullup_43_out), .D(pullup_45_out), .S(nfet_92_s));
  PullUp pullup_46 (.out(nfet_90_d));
  NFET nfet_93 (.G(nfet_90_d), .D(nfet_92_s), .S(1'b0));
  PullUp pullup_47 (.out(pullup_47_out));
  NFET nfet_94 (.G(CLK_2), .D(pullup_47_out), .S(1'b0));
  PullUp pullup_48 (.out(pullup_48_out));
  NFET nfet_95 (.G(pullup_47_out), .D(pullup_48_out), .S(nfet_95_s));
  NFET nfet_96 (.G(pullup_43_out), .D(nfet_95_s), .S(1'b0));
  PullUp pullup_49 (.out(pullup_49_out));
  NFET nfet_97 (.G(Qout), .D(pullup_49_out), .S(nfet_97_s));
  NFET nfet_98 (.G(pullup_48_out), .D(nfet_97_s), .S(1'b0));
  PullUp pullup_50 (.out(pullup_50_out));
  NFET nfet_99 (.G(pullup_50_out), .D(nfet_99_d), .S(1'b0));
  NFET nfet_100 (.G(pullup_47_out), .D(pullup_50_out), .S(nfet_100_s));
  NFET nfet_101 (.G(pullup_45_out), .D(nfet_100_s), .S(1'b0));
  PullUp pullup_51 (.out(Qout));
  NFET nfet_102 (.G(pullup_49_out), .D(Qout), .S(nfet_99_d));

  // Notes on the sheet:
  //   NMOS FET 2:1 MUX (6 TR, 4R)
  //   NMOS FET NAND
  //   NMOS FET Half Adder
  //   NMOS FET Full-Adder (16 TR, 7 R)
  //   NMOS FET XOR
  //   NMOS FET NOR
  //   NMOS FET ALU Slice 
  //    (46 Transistors, 23 Resistors)
  //   NMOS FET Master-Slave Flip-Flop (17 TR, 9 R)
  //   NMOS FET 2:1 MUX
  //   Carry Suppress
endmodule
